# Fritzing sketch Schematic (saved by Fritzing 0.8.5b)

parts:
  Launchpad1 = TI Launchpad MSP430G2
  Braille_DOT1 = SPEAKER [package=pcb_mount_speaker]
  Braille_DOT5 = SPEAKER [package=pcb_mount_speaker]
  Braille_DOT3 = SPEAKER [package=pcb_mount_speaker]
  Braille_DOT4 = SPEAKER [package=pcb_mount_speaker]
  Braille_DOT6 = SPEAKER [package=pcb_mount_speaker]
  Braille_DOT2 = SPEAKER [package=pcb_mount_speaker]

nets:
  N1: Launchpad1.p10, Braille_DOT3.-
  N2: Launchpad1.p9, Braille_DOT2.-
  N3: Launchpad1.p7, Braille_DOT6.-
  N4: Launchpad1.p6, Braille_DOT5.-
  N5: Launchpad1.p5, Braille_DOT4.-
  N6: Launchpad1.p2, Braille_DOT1.-
