# Fritzing sketch Schematic_LEDs (saved by Fritzing 0.8.5b)
breadboards: 1

parts:
  LED1 = LED - 5mm [color="Red (633nm)" package="5 mm [THT]"]
  LED2 = LED - 5mm [color="Red (633nm)" package="5 mm [THT]"]
  LED3 = LED - 5mm [color="Red (633nm)" package="5 mm [THT]"]
  LED4 = LED - 5mm [color="Red (633nm)" package="5 mm [THT]"]
  LED5 = LED - 5mm [color="Red (633nm)" package="5 mm [THT]"]
  LED6 = LED - 5mm [color="Red (633nm)" package="5 mm [THT]"]
  Launchpad1 = TI Launchpad MSP430G2

nets:
  N1: LED1.cathode, LED2.cathode, LED3.cathode, LED4.cathode, LED5.cathode, LED6.cathode, Launchpad1.p20
  N2: LED1.anode, Launchpad1.p2
  N3: LED2.anode, Launchpad1.p9
  N4: LED3.anode, Launchpad1.p6
  N5: LED4.anode, Launchpad1.p5
  N6: LED5.anode, Launchpad1.p10
  N7: LED6.anode, Launchpad1.p7
